# Fritzing sketch coffeetime (saved by Fritzing 0.9.2b)
breadboards: 1

parts:
  U1 = RELAY [package=relay-jzc]
  Q2 = NPN-Transistor [package="TO92 [THT]"]
  Part1 = Arduino Uno (Rev3)
  R1 = Resistor [tolerance=±5% resistance=1k package="0603 [SMD]"]
  D1 = Diode [package=diode-hv]

nets:
  N1: U1.COIL2, Q2.C, D1.A
  N2: U1.NO, Part1.5V
  N3: Q2.E, Part1.GND
  N4: Q2.B, R1.Pin_1
  N5: Part1.D8, R1.Pin_0

notes:
  NPN BD135 (ECB)
  R = 1KOHM
  Phase of Coffee Machine
